// Logisim project 10.Ula8Bits.circ as structural Verilog: 10 circuits, main circuit main
module main (
  input  [7:0] A,
  input  [7:0] B,
  input  [3:0] in_3,
  output [7:0] Saida,
  output out_5,
  output out_6
);

  wire [7:0] and_1_out, nand_1_out, nor_1_out, not_1_out, or_1_out, shift2dir_1_saida, shift2esq_1_saida,
       somadorfinal_1_saida, subtrator8bits_1_saida, xor_1_out;

  assign nand_1_out = ~(A & B);  // NAND_Gate nand_1, 8 bits wide
  assign and_1_out = A & B;  // AND_Gate and_1, 8 bits wide
  assign nor_1_out = ~(A | B);  // NOR_Gate nor_1, 8 bits wide
  assign xor_1_out = A ^ B;  // XOR_Gate xor_1, 8 bits wide
  assign or_1_out = A | B;  // OR_Gate or_1, 8 bits wide
  assign not_1_out = ~A;  // NOT_Gate not_1, 8 bits wide
  somadorfinal somadorfinal_1 (.A(A), .B(B), .Cout(out_5), .Saida(somadorfinal_1_saida));
  subtrator8bits subtrator8bits_1 (.Minuendo(A), .Subtraendo(B), .Sinal(out_6), .Saida(subtrator8bits_1_saida));
  shift2esq shift2esq_1 (.entrada(A), .saida(shift2esq_1_saida));
  shift2dir shift2dir_1 (.entrada(A), .saida(shift2dir_1_saida));
  multip16ent8bits multip16ent8bits_1 (
    .I0(nand_1_out), .I1(and_1_out), .I2(nor_1_out), .I3(xor_1_out), .I4(or_1_out), .I5(not_1_out),
    .I6(somadorfinal_1_saida), .I7(subtrator8bits_1_saida), .I8(shift2esq_1_saida), .I9(shift2dir_1_saida),
    .Sel(in_3), .out_18(Saida));  // open: I10, I11, I12, I13, I14, I15

  // Notes on the sheet:
  //   nand
  //   and
  //   nor
  //   xor
  //   or 
  //   not
endmodule

module somador1bit (
  input  a0,
  input  a1,
  input  cin,
  output s,
  output cout
);

  wire and_1_out, and_2_out, and_3_out, xor_1_out;

  xor xor_1 (xor_1_out, a0, a1);
  and and_1 (and_1_out, a0, a1);
  and and_2 (and_2_out, a1, cin);
  and and_3 (and_3_out, a0, cin);
  xor xor_2 (s, xor_1_out, cin);
  or or_1 (cout, and_1_out, and_2_out, and_3_out);
endmodule

module somador4bits (
  input  carryin,
  input  in_2,
  input  in_3,
  input  in_4,
  input  in_5,
  input  in_6,
  input  in_7,
  input  in_8,
  input  in_9,
  output c3,
  output c2,
  output c1,
  output c0,
  output cout_Overflow_ed7af212
);

  wire somador1bit_2_cout, somador1bit_3_cout, somador1bit_4_cout;

  somador1bit somador1bit_1 (.a1(in_6), .cin(somador1bit_2_cout), .a0(in_2), .s(c3), .cout(cout_Overflow_ed7af212));
  somador1bit somador1bit_2 (.a1(in_7), .cin(somador1bit_3_cout), .a0(in_3), .s(c2), .cout(somador1bit_2_cout));
  somador1bit somador1bit_3 (.a1(in_8), .cin(somador1bit_4_cout), .a0(in_4), .s(c1), .cout(somador1bit_3_cout));
  somador1bit somador1bit_4 (.a1(in_9), .cin(carryin), .a0(in_5), .s(c0), .cout(somador1bit_4_cout));
endmodule

module somador8bits (
  input  in_1,
  input  in_2,
  input  in_3,
  input  in_4,
  input  in_5,
  input  in_6,
  input  in_7,
  input  in_8,
  input  in_9,
  input  in_10,
  input  in_11,
  input  in_12,
  input  in_13,
  input  in_14,
  input  in_15,
  input  in_16,
  input  in_17,
  output out_18,
  output out_19,
  output out_20,
  output Resultado,
  output out_22,
  output out_23,
  output out_24,
  output out_25,
  output Overflow
);

  wire somador4bits_1_cout_overflow_ed7af212;

  somador4bits somador4bits_1 (
    .in_6(in_16), .in_2(in_14), .in_7(in_12), .in_3(in_10), .in_8(in_8), .in_4(in_6), .carryin(in_1),
    .in_9(in_4), .in_5(in_2), .cout_Overflow_ed7af212(somador4bits_1_cout_overflow_ed7af212), .c3(out_22),
    .c2(out_23), .c1(out_24), .c0(out_25));
  somador4bits somador4bits_2 (
    .in_6(in_17), .in_2(in_15), .in_7(in_13), .in_3(in_11), .in_8(in_9), .in_4(in_7),
    .carryin(somador4bits_1_cout_overflow_ed7af212), .in_9(in_5), .in_5(in_3),
    .cout_Overflow_ed7af212(Overflow), .c3(out_18), .c2(out_19), .c1(out_20), .c0(Resultado));
endmodule

module somadorfinal (
  input  [7:0] A,
  input  [7:0] B,
  output Cout,
  output [7:0] Saida
);

  somador8bits somador8bits_1 (
    .in_4(B[0]), .in_6(A[1]), .in_8(B[1]), .in_10(A[2]), .in_12(B[2]), .in_14(A[3]), .in_16(B[3]),
    .in_2(A[0]), .in_1(1'b0), .in_5(B[4]), .in_7(A[5]), .in_9(B[5]), .in_11(A[6]), .in_13(B[6]),
    .in_15(A[7]), .in_17(B[7]), .in_3(A[4]), .out_18(Saida[7]), .out_19(Saida[6]), .out_20(Saida[5]),
    .Resultado(Saida[4]), .out_22(Saida[3]), .out_23(Saida[2]), .out_24(Saida[1]), .out_25(Saida[0]),
    .Overflow(Cout));

  // Notes on the sheet:
  //   Overflow?
endmodule

module subtrator8bits (
  input  [7:0] Minuendo,
  input  [7:0] Subtraendo,
  output Sinal,
  output [7:0] Saida
);

  wire not_1_out, not_2_out, not_3_out, not_4_out, not_5_out, not_6_out, not_7_out, not_8_out;

  not not_1 (not_1_out, Subtraendo[0]);
  not not_2 (not_2_out, Subtraendo[1]);
  not not_3 (not_3_out, Subtraendo[2]);
  not not_4 (not_4_out, Subtraendo[3]);
  not not_5 (not_5_out, Subtraendo[4]);
  not not_6 (not_6_out, Subtraendo[5]);
  not not_7 (not_7_out, Subtraendo[6]);
  not not_8 (not_8_out, Subtraendo[7]);
  somador8bits somador8bits_1 (
    .in_4(not_1_out), .in_6(Minuendo[1]), .in_8(not_2_out), .in_10(Minuendo[2]), .in_12(not_3_out),
    .in_14(Minuendo[3]), .in_16(not_4_out), .in_2(Minuendo[0]), .in_1(1'b1), .in_5(not_5_out),
    .in_7(Minuendo[5]), .in_9(not_6_out), .in_11(Minuendo[6]), .in_13(not_7_out), .in_15(Minuendo[7]),
    .in_17(not_8_out), .in_3(Minuendo[4]), .out_18(Saida[7]), .out_19(Saida[6]), .out_20(Saida[5]),
    .Resultado(Saida[4]), .out_22(Saida[3]), .out_23(Saida[2]), .out_24(Saida[1]), .out_25(Saida[0]),
    .Overflow(Sinal));

  // Notes on the sheet:
  //   Overflow?
endmodule

module shift2esq (
  input  [7:0] entrada,
  output [7:0] saida
);


  assign saida = {entrada[5:0], 2'b00};
endmodule

module shift2dir (
  input  [7:0] entrada,
  output [7:0] saida
);


  assign saida = {2'b00, entrada[7:2]};
endmodule

module multip16ent (
  input  [3:0] sel,
  input  a,
  input  b,
  input  c,
  input  d,
  input  e,
  input  f,
  input  g,
  input  h,
  input  i,
  input  j,
  input  k,
  input  l,
  input  m,
  input  n,
  input  o,
  input  p,
  output out_18
);

  wire and_1_out, and_2_out, and_3_out, and_4_out, and_5_out, and_6_out, and_7_out, and_8_out, and_9_out,
       and_10_out, and_11_out, and_12_out, and_13_out, and_14_out, and_15_out, and_16_out, not_1_out,
       not_2_out, not_3_out, not_4_out;

  not not_1 (not_1_out, sel[3]);
  not not_2 (not_2_out, sel[2]);
  not not_3 (not_3_out, sel[1]);
  not not_4 (not_4_out, sel[0]);
  and and_1 (and_1_out, a, not_4_out, not_3_out, not_2_out, not_1_out);
  and and_2 (and_2_out, b, sel[0], not_3_out, not_2_out, not_1_out);
  and and_3 (and_3_out, c, not_4_out, sel[1], not_2_out, not_1_out);
  and and_4 (and_4_out, d, sel[0], sel[1], not_2_out, not_1_out);
  and and_5 (and_5_out, e, not_4_out, not_3_out, sel[2], not_1_out);
  and and_6 (and_6_out, f, sel[0], not_3_out, sel[2], not_1_out);
  and and_7 (and_7_out, g, not_4_out, sel[1], sel[2], not_1_out);
  and and_8 (and_8_out, h, sel[0], sel[1], sel[2], not_1_out);
  and and_9 (and_9_out, i, not_4_out, not_3_out, not_2_out, sel[3]);
  and and_10 (and_10_out, j, sel[0], not_3_out, not_2_out, sel[3]);
  and and_11 (and_11_out, k, not_4_out, sel[1], not_2_out, sel[3]);
  and and_12 (and_12_out, l, sel[0], sel[1], not_2_out, sel[3]);
  and and_13 (and_13_out, m, not_4_out, not_3_out, sel[2], sel[3]);
  and and_14 (and_14_out, n, sel[0], not_3_out, sel[2], sel[3]);
  and and_15 (and_15_out, o, not_4_out, sel[1], sel[2], sel[3]);
  and and_16 (and_16_out, p, sel[0], sel[1], sel[2], sel[3]);
  or or_1 (out_18, and_1_out, and_2_out, and_3_out, and_4_out, and_5_out, and_6_out, and_7_out, and_8_out, and_9_out, and_10_out, and_11_out, and_12_out, and_13_out, and_14_out, and_15_out, and_16_out);
endmodule

module multip16ent8bits (
  input  [7:0] I0,
  input  [7:0] I1,
  input  [7:0] I2,
  input  [7:0] I3,
  input  [7:0] I4,
  input  [7:0] I5,
  input  [7:0] I6,
  input  [7:0] I7,
  input  [7:0] I8,
  input  [7:0] I9,
  input  [7:0] I10,
  input  [7:0] I11,
  input  [7:0] I12,
  input  [7:0] I13,
  input  [7:0] I14,
  input  [7:0] I15,
  input  [3:0] Sel,
  output [7:0] out_18
);

  multip16ent multip16ent_1 (
    .o(I14[0]), .p(I15[0]), .a(I0[0]), .b(I1[0]), .c(I2[0]), .d(I3[0]), .e(I4[0]), .f(I5[0]), .g(I6[0]),
    .h(I7[0]), .i(I8[0]), .j(I9[0]), .k(I10[0]), .l(I11[0]), .m(I12[0]), .n(I13[0]), .sel(Sel),
    .out_18(out_18[0]));
  multip16ent multip16ent_2 (
    .o(I14[1]), .p(I15[1]), .a(I0[1]), .b(I1[1]), .c(I2[1]), .d(I3[1]), .e(I4[1]), .f(I5[1]), .g(I6[1]),
    .h(I7[1]), .i(I8[1]), .j(I9[1]), .k(I10[1]), .l(I11[1]), .m(I12[1]), .n(I13[1]), .sel(Sel),
    .out_18(out_18[1]));
  multip16ent multip16ent_3 (
    .o(I14[2]), .p(I15[2]), .a(I0[2]), .b(I1[2]), .c(I2[2]), .d(I3[2]), .e(I4[2]), .f(I5[2]), .g(I6[2]),
    .h(I7[2]), .i(I8[2]), .j(I9[2]), .k(I10[2]), .l(I11[2]), .m(I12[2]), .n(I13[2]), .sel(Sel),
    .out_18(out_18[2]));
  multip16ent multip16ent_4 (
    .o(I14[3]), .p(I15[3]), .a(I0[3]), .b(I1[3]), .c(I2[3]), .d(I3[3]), .e(I4[3]), .f(I5[3]), .g(I6[3]),
    .h(I7[3]), .i(I8[3]), .j(I9[3]), .k(I10[3]), .l(I11[3]), .m(I12[3]), .n(I13[3]), .sel(Sel),
    .out_18(out_18[3]));
  multip16ent multip16ent_5 (
    .o(I14[4]), .p(I15[4]), .a(I0[4]), .b(I1[4]), .c(I2[4]), .d(I3[4]), .e(I4[4]), .f(I5[4]), .g(I6[4]),
    .h(I7[4]), .i(I8[4]), .j(I9[4]), .k(I10[4]), .l(I11[4]), .m(I12[4]), .n(I13[4]), .sel(Sel),
    .out_18(out_18[4]));
  multip16ent multip16ent_6 (
    .o(I14[5]), .p(I15[5]), .a(I0[5]), .b(I1[5]), .c(I2[5]), .d(I3[5]), .e(I4[5]), .f(I5[5]), .g(I6[5]),
    .h(I7[5]), .i(I8[5]), .j(I9[5]), .k(I10[5]), .l(I11[5]), .m(I12[5]), .n(I13[5]), .sel(Sel),
    .out_18(out_18[5]));
  multip16ent multip16ent_7 (
    .o(I14[6]), .p(I15[6]), .a(I0[6]), .b(I1[6]), .c(I2[6]), .d(I3[6]), .e(I4[6]), .f(I5[6]), .g(I6[6]),
    .h(I7[6]), .i(I8[6]), .j(I9[6]), .k(I10[6]), .l(I11[6]), .m(I12[6]), .n(I13[6]), .sel(Sel),
    .out_18(out_18[6]));
  multip16ent multip16ent_8 (
    .o(I14[7]), .p(I15[7]), .a(I0[7]), .b(I1[7]), .c(I2[7]), .d(I3[7]), .e(I4[7]), .f(I5[7]), .g(I6[7]),
    .h(I7[7]), .i(I8[7]), .j(I9[7]), .k(I10[7]), .l(I11[7]), .m(I12[7]), .n(I13[7]), .sel(Sel),
    .out_18(out_18[7]));
endmodule
