// Logisim project 12.MaquinaDeEstados.circ as structural Verilog
module Latch (
  input  S,
  input  R,
  output Q,
  output Qb
);

  nand nand_1 (Q, S, Qb);
  nand nand_2 (Qb, Q, R);
endmodule

module flipflopD (
  input  D,
  input  Clk,
  output Q,
  output Qb
);

  wire latch_1_q, nand_1_out, nand_2_out, nand_3_out, nand_4_out, not_1_out, not_2_out, not_3_out;

  not not_1 (not_1_out, D);
  not not_2 (not_2_out, Clk);
  nand nand_1 (nand_1_out, D, Clk);
  nand nand_2 (nand_2_out, Clk, not_1_out);
  Latch latch_1 (.S(nand_1_out), .R(nand_2_out), .Q(latch_1_q));  // open: Qb
  not not_3 (not_3_out, latch_1_q);
  nand nand_3 (nand_3_out, latch_1_q, not_2_out);
  nand nand_4 (nand_4_out, not_2_out, not_3_out);
  Latch latch_2 (.S(nand_3_out), .R(nand_4_out), .Q(Q), .Qb(Qb));
endmodule

module flipflopJK (
  input  J,
  input  K,
  input  Clk,
  output Q,
  output Qb
);

  wire and_1_out, and_2_out, or_1_out;

  and and_1 (and_1_out, Qb, J);
  and and_2 (and_2_out, ~K, Q);  // AND_Gate
  or or_1 (or_1_out, and_1_out, and_2_out);
  flipflopD flipflopd_1 (.D(or_1_out), .Clk(Clk), .Q(Q), .Qb(Qb));
endmodule

module maquinaDeEstados (
  input  entradaX,
  input  Clk,
  output saidaY
);

  wire and_1_out, and_2_out, flipflopd_1_q, flipflopd_2_q, not_1_out, not_2_out, or_1_out;

  not not_1 (not_1_out, flipflopd_2_q);
  not not_2 (not_2_out, entradaX);
  and and_1 (and_1_out, flipflopd_1_q, not_1_out, entradaX);
  and and_2 (and_2_out, flipflopd_2_q, not_2_out);
  or or_1 (or_1_out, and_1_out, and_2_out);
  flipflopD flipflopd_1 (.D(or_1_out), .Clk(Clk), .Q(flipflopd_1_q));  // open: Qb
  flipflopD flipflopd_2 (.D(entradaX), .Clk(Clk), .Q(flipflopd_2_q));  // open: Qb
  and and_3 (saidaY, flipflopd_1_q, flipflopd_2_q);
endmodule
