// Logisim project 7.Bancode4Registradores8bits.circ as structural Verilog: 6 circuits, main circuit main
module main (
  input  [1:0] Sel,
  input  Clk,
  input  [7:0] Entrada,
  output [7:0] LeituraReg
);

  wire a00_out, a01_out, a10_out, a11_out, and_1_out, and_2_out, and_3_out, and_4_out, not_1_out, not_2_out,
       not_3_out, not_4_out;
  wire [7:0] reg8bits_1_saida, reg8bits_2_saida, reg8bits_3_saida, reg8bits_4_saida;

  not not_1 (not_1_out, Sel[1]);
  not not_2 (not_2_out, Sel[0]);
  not not_3 (not_3_out, Sel[1]);
  not not_4 (not_4_out, Sel[0]);
  and a00 (a00_out, not_1_out, not_2_out);
  and a01 (a01_out, not_3_out, Sel[0]);
  and a10 (a10_out, Sel[1], not_4_out);
  and a11 (a11_out, Sel[1], Sel[0]);
  and and_1 (and_1_out, Clk, a00_out);
  and and_2 (and_2_out, Clk, a01_out);
  and and_3 (and_3_out, Clk, a10_out);
  and and_4 (and_4_out, Clk, a11_out);
  reg8bits reg8bits_1 (.Clock(and_1_out), .Entrada(Entrada), .Saida(reg8bits_1_saida));
  reg8bits reg8bits_2 (.Clock(and_2_out), .Entrada(Entrada), .Saida(reg8bits_2_saida));
  reg8bits reg8bits_3 (.Clock(and_3_out), .Entrada(Entrada), .Saida(reg8bits_3_saida));
  reg8bits reg8bits_4 (.Clock(and_4_out), .Entrada(Entrada), .Saida(reg8bits_4_saida));
  multiplexador8bits multiplexador8bits_1 (
    .a11(reg8bits_4_saida), .a10(reg8bits_3_saida), .Sel(Sel), .a01(reg8bits_2_saida),
    .a00(reg8bits_1_saida), .s(LeituraReg));
endmodule

module srlatch (
  input  in_1,
  input  in_2,
  output out_3,
  output out_4
);

  nand nand_1 (out_3, in_1, out_4);
  nand nand_2 (out_4, out_3, in_2);
endmodule

module dflipflop (
  input  D,
  input  Clk,
  output Q,
  output Qb
);

  wire nand_1_out, nand_2_out, nand_3_out, nand_4_out, not_1_out, not_2_out, not_3_out, srlatch_1_out_3;

  not not_1 (not_1_out, D);
  nand nand_1 (nand_1_out, D, Clk);
  nand nand_2 (nand_2_out, Clk, not_1_out);
  not not_2 (not_2_out, Clk);
  srlatch srlatch_1 (.in_1(nand_1_out), .in_2(nand_2_out), .out_3(srlatch_1_out_3));  // open: out_4
  not not_3 (not_3_out, srlatch_1_out_3);
  nand nand_3 (nand_3_out, srlatch_1_out_3, not_2_out);
  nand nand_4 (nand_4_out, not_2_out, not_3_out);
  srlatch srlatch_2 (.in_1(nand_3_out), .in_2(nand_4_out), .out_3(Q), .out_4(Qb));
endmodule

module reg8bits (
  input  Clock,
  input  [7:0] Entrada,
  output [7:0] Saida
);

  dflipflop dflipflop_1 (.Clk(Clock), .D(Entrada[7]), .Q(Saida[7]));  // open: Qb
  dflipflop dflipflop_2 (.Clk(Clock), .D(Entrada[6]), .Q(Saida[6]));  // open: Qb
  dflipflop dflipflop_3 (.Clk(Clock), .D(Entrada[5]), .Q(Saida[5]));  // open: Qb
  dflipflop dflipflop_4 (.Clk(Clock), .D(Entrada[4]), .Q(Saida[4]));  // open: Qb
  dflipflop dflipflop_5 (.Clk(Clock), .D(Entrada[3]), .Q(Saida[3]));  // open: Qb
  dflipflop dflipflop_6 (.Clk(Clock), .D(Entrada[2]), .Q(Saida[2]));  // open: Qb
  dflipflop dflipflop_7 (.Clk(Clock), .D(Entrada[1]), .Q(Saida[1]));  // open: Qb
  dflipflop dflipflop_8 (.Clk(Clock), .D(Entrada[0]), .Q(Saida[0]));  // open: Qb
endmodule

module multiplexador4entradas (
  input  [1:0] sel,
  input  a,
  input  b,
  input  c,
  input  d,
  output out_6
);

  wire and_1_out, and_2_out, and_3_out, and_4_out, not_1_out, not_2_out;

  not not_1 (not_1_out, sel[1]);
  not not_2 (not_2_out, sel[0]);
  and and_1 (and_1_out, a, not_2_out, not_1_out);
  and and_2 (and_2_out, b, sel[0], not_1_out);
  and and_3 (and_3_out, c, not_2_out, sel[1]);
  and and_4 (and_4_out, d, sel[0], sel[1]);
  or or_1 (out_6, and_1_out, and_2_out, and_3_out, and_4_out);
endmodule

module multiplexador8bits (
  input  [7:0] a11,
  input  [7:0] a10,
  input  [7:0] a01,
  input  [7:0] a00,
  input  [1:0] Sel,
  output [7:0] s
);

  multiplexador4entradas multiplexador4entradas_1 (
    .sel(Sel), .a(a00[0]), .b(a01[0]), .c(a10[0]), .d(a11[0]), .out_6(s[0]));
  multiplexador4entradas multiplexador4entradas_2 (
    .sel(Sel), .a(a00[1]), .b(a01[1]), .c(a10[1]), .d(a11[1]), .out_6(s[1]));
  multiplexador4entradas multiplexador4entradas_3 (
    .sel(Sel), .a(a00[2]), .b(a01[2]), .c(a10[2]), .d(a11[2]), .out_6(s[2]));
  multiplexador4entradas multiplexador4entradas_4 (
    .sel(Sel), .a(a00[3]), .b(a01[3]), .c(a10[3]), .d(a11[3]), .out_6(s[3]));
  multiplexador4entradas multiplexador4entradas_5 (
    .sel(Sel), .a(a00[4]), .b(a01[4]), .c(a10[4]), .d(a11[4]), .out_6(s[4]));
  multiplexador4entradas multiplexador4entradas_6 (
    .sel(Sel), .a(a00[5]), .b(a01[5]), .c(a10[5]), .d(a11[5]), .out_6(s[5]));
  multiplexador4entradas multiplexador4entradas_7 (
    .sel(Sel), .a(a00[6]), .b(a01[6]), .c(a10[6]), .d(a11[6]), .out_6(s[6]));
  multiplexador4entradas multiplexador4entradas_8 (
    .sel(Sel), .a(a00[7]), .b(a01[7]), .c(a10[7]), .d(a11[7]), .out_6(s[7]));
endmodule
